# Fritzing sketch ProjectOne_electronica (saved by Fritzing 0.9.4)
breadboards: 2

parts:
  Raspberry_Pi = Raspberry Pi 4 [part_number=RPI-4-b]
  SPI_MCP = MCP3008 [package=dil16]
  S1 = SWITCH-MOMENTARY-2 [package=tactile-pth-12mm]
  S2 = SWITCH-MOMENTARY-2 [package=tactile-pth-12mm]
  LCD_met_I2C = LCD1602-I2C
  Temperatuursensor_DS = DS18B20 1-Wire Temperature Sensor [part_number=DS18B20]
  Alcoholsensor = GAS_SENSOR [package=mq-3]
  PowerSupply = YwRobot Breadboard Power Supply [part_number=545043]
  R1 = Resistor [tolerance=±5% resistance=330 package=THT]
  R2 = Resistor [tolerance=±5% resistance=330 package=THT]
  RFID = RFID-RC522-v2
  T-stuk_GPIO = Adafruit T-Cobbler Plus [part_number="Adafruit #1989 and #2028"]
  Relais = KY-019 5V Relay Module [package="Breakout board"]
  R3 = Resistor [tolerance=±5% resistance=330 package=THT]
  J1 = Piezo Speaker

nets:
  3V3: Raspberry_Pi.3v3, Raspberry_Pi.3V3, T-stuk_GPIO.+3.3V, T-stuk_GPIO.+3.3V_2, R3.Pin_1
  N1: Raspberry_Pi.GPIO2, LCD_met_I2C.SDA, T-stuk_GPIO.SDA, J1.pin2
  N2: Raspberry_Pi.GPIO3, LCD_met_I2C.SCL, T-stuk_GPIO.SCL
  N3: Raspberry_Pi.GPIO4, Temperatuursensor_DS.DQ, T-stuk_GPIO.GPIO4, R3.Pin_0
  GND: Raspberry_Pi.GND, SPI_MCP.DGND, LCD_met_I2C.GND, Alcoholsensor.H2, T-stuk_GPIO.GND, Relais.-, J1.pin1
  N4: Raspberry_Pi.GPIO17, T-stuk_GPIO.GPIO17
  N5: Raspberry_Pi.GPIO27, T-stuk_GPIO.GPIO27
  N6: Raspberry_Pi.GPIO22, T-stuk_GPIO.GPIO22
  N7: Raspberry_Pi.GPIO10, SPI_MCP.Din, RFID.MOSI, T-stuk_GPIO.MOSI
  N8: Raspberry_Pi.GPIO9, SPI_MCP.Dout, RFID.MISO, T-stuk_GPIO.MISO
  N9: Raspberry_Pi.GPIO11, SPI_MCP.CLK, RFID.SCK, T-stuk_GPIO.SCLK
  N10: Raspberry_Pi.ID_SD, T-stuk_GPIO.EEDAT
  N11: Raspberry_Pi.GPIO5, T-stuk_GPIO.GPIO5
  N12: Raspberry_Pi.GPIO6, T-stuk_GPIO.GPIO6
  N13: Raspberry_Pi.GPIO13, T-stuk_GPIO.GPIO13
  N14: Raspberry_Pi.GPIO19, T-stuk_GPIO.GPIO19
  N15: Raspberry_Pi.GPIO26, T-stuk_GPIO.GPIO26
  N16: Raspberry_Pi.GPIO21, T-stuk_GPIO.GPIO21
  N17: Raspberry_Pi.GPIO20, T-stuk_GPIO.GPIO20
  N18: Raspberry_Pi.GPIO16, T-stuk_GPIO.GPIO16
  N19: Raspberry_Pi.GPIO12, T-stuk_GPIO.GPIO12
  N20: Raspberry_Pi.ID_SC, T-stuk_GPIO.EECLK
  N21: Raspberry_Pi.GPIO7, RFID.SDA, T-stuk_GPIO.CE1
  N22: Raspberry_Pi.GPIO8, SPI_MCP.CS/SHDN, T-stuk_GPIO.CE0
  N23: Raspberry_Pi.GPIO25, T-stuk_GPIO.GPIO25
  N24: Raspberry_Pi.GPIO24, T-stuk_GPIO.GPIO24, Relais.S
  N25: Raspberry_Pi.GPIO23, R1.Pin_0, T-stuk_GPIO.GPIO23
  N26: Raspberry_Pi.GPIO18, R2.Pin_0, T-stuk_GPIO.GPIO18
  N27: Raspberry_Pi.GPIO15, T-stuk_GPIO.RXD
  N28: Raspberry_Pi.GPIO14, T-stuk_GPIO.TXD
  5V: Raspberry_Pi.5V, T-stuk_GPIO.+5V
  N29: SPI_MCP.CH1, Alcoholsensor.A1
  GND_2: SPI_MCP.AGND, S1.2, S2.2, Temperatuursensor_DS.GND, PowerSupply.GND
  VDD: SPI_MCP.VREF, SPI_MCP.VDD, LCD_met_I2C.VCC, Alcoholsensor.H1, RFID.3.3V, Relais.+
  N30: S1.1, R1.Pin_1
  N31: S2.1, R2.Pin_1
  N32: Temperatuursensor_DS.VDD, PowerSupply.VCC#5

custom parts:
  Raspberry Pi 4: The RPi4, a faster version of the awesome Raspberry Pi 2 B ARM Board with 40 pin gpio. Ready for special Raspberry Pi B+ and RPi2 Hat (Hardware attached (on) top)
  LCD1602-I2C: A standard character display, usually with 2x16 characters. Comes in many colors with LCM1602 IIC attached.
  YwRobot Breadboard Power Supply: The YwRobot Breadboard Power Supply (MB-V2) has two power rails; they can be 5V or 3V3. Power to the module can be provided through the female USB socket or through the A10 (female) 2.1mm power jack.
  RFID-RC522-v2: A simple China made RFID-RC522 Reader; do check the pin labels, as this is a MFRC522 based clone.
  Adafruit T-Cobbler Plus: The Raspberry Pi has landed on the Maker World like a 40-GPIO pinned, quad-USB ported, credit card sized bomb of DIY joy. And while you can use most of our great Model B accessories by hooking up our downgrade cable, its probably a good time to upgrade your set up and accessorize using all of the 40 pins. That's why we now carry the Assembled Adafruit Pi T-Cobbler Plus - Breakout + Cable for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
  KY-019 5V Relay Module: KY-019 5V Relay module, used to control AC circuits. (Special thanks to vanepp for fixing the PCB holes and other errors)
